# Fritzing sketch schematic (saved by Fritzing 0.9.3b)

parts:
  Part1 = Arduino Uno (Rev3)
  J1 = Basic Servo
  RFID1 = RFID Reader
  RFID2 = RFID Reader
  LED1 = LED - 5mm [color="Red (633nm)" package="5 mm [THT]"]
  LED2 = LED - 5mm [color="Red (633nm)" package="5 mm [THT]"]
  V1 = DC Power [voltage=5]  # not connected

nets:
  N1: Part1.A0, RFID1.ANT0
  N2: Part1.A1, RFID2.ANT0
  GND: Part1.GND, J1.gnd, RFID1.GND, RFID2.GND, LED1.anode, LED2.anode
  N3: Part1.D2, J1.pulse
  5V: Part1.5V, RFID2.+5V, LED1.cathode, LED2.cathode
